# Fritzing sketch Breathing Sensor Fritz (saved by Fritzing 0.8.3b)
breadboards: 1

parts:
  Part1 = Arduino Fio (Funnel I/O)
  R1 = Textile Stretch Sensor [part_number=PW052]
  R2 = Resistor [tolerance=±5% resistance=10k package=THT]
  U2 = LIPO-2000mAh [package=lipo-2000]  # not connected
  U1 = XBee  # not connected

nets:
  N1: Part1.GND, R1.pin_1
  N2: Part1.VCC, R2.Pin_0
  N3: Part1.A0, R1.pin_0, R2.Pin_1
